# Fritzing sketch module (saved by Fritzing 0.9.3b)
circuit board: 8.46667cm x 5.64444cm
breadboards: 1

parts:
  Part1 = Arduino Uno (Rev3)
  RHT1 = Humidity and Temperature Sensor RHT03

nets:
  N1: Part1.GND, RHT1.GND_1
  N2: Part1.D2, RHT1.Data-signal
  5V: Part1.5V, RHT1.Vcc
